// Logisim project DFF.circ as structural Verilog: 1 circuit, main circuit main
module main (
  input  in_1,
  input  in_2,
  input  in_3,
  input  in_4,
  output out_5,
  output out_6,
  output out_7,
  output out_8
);

  wire clock_1_out, d_ff_1_q;
  wire [7:1] rom_1_data, undriven;

  Clock clock_1 (.out(clock_1_out));
  D_Flip_Flop d_ff_1 (.clk(clock_1_out), .D(in_1), .Q(d_ff_1_q));  // open: Qn, preset, en, reset
  D_Flip_Flop d_ff_2 (.clk(clock_1_out), .D(d_ff_1_q), .Q(out_5));  // open: Qn, preset, en, reset
  ROM rom_1 (.addr({undriven, in_4}), .data({rom_1_data, out_7}), .sel(out_8));
  and and_1 (out_6, in_2, in_3);
  // Pins of 1 and 8 bits meet at {undriven, in_4}
  // Pins of 1 and 8 bits meet at {rom_1_data, out_7}
endmodule
