// Logisim project MUX.circ as structural Verilog: 1 circuit, main circuit main
module main (
  input  in_1,
  input  in_2,
  input  in_3,
  input  in_4,
  input  in_5,
  input  in_6,
  input  in_7,
  input  in_8,
  input  in_9,
  input  in_10,
  input  in_11,
  input  in_12,
  input  [2:0] in_13,
  input  in_14,
  input  in_15,
  input  in_16,
  input  in_17,
  input  [1:0] Selector,
  output out_19,
  output out_20,
  output RES
);

  Multiplexer multiplexer_1 (.in0(in_3), .in1(in_5), .out(out_19), .sel(in_9), .en(in_10));
  Multiplexer #(.select(2), .disabled(0)) multiplexer_2 (
    .in0(in_14), .in1(in_15), .in2(in_16), .in3(in_17), .out(RES), .sel(Selector));  // open: en
  Multiplexer #(.select(3)) multiplexer_3 (
    .in0(in_1), .in1(in_2), .in2(in_4), .in3(in_6), .in4(in_7), .in5(in_8), .in6(in_11), .in7(in_12),
    .out(out_20), .sel(in_13));  // open: en
endmodule
